# Fritzing sketch ultrasonic (saved by Fritzing 0.9.4)
breadboards: 1

parts:
  HC-SR04_Sensor_1 = HC-SR04 Ultrasonic Distance Sensor
  J1 = Piezo Speaker
  LED1 = smd LED [color="Red (633nm)" package="0603 [SMD]"]
  LED2 = smd LED [color="Red (633nm)" package="0603 [SMD]"]
  LED3 = smd LED [color="Red (633nm)" package="0603 [SMD]"]
  Part1 = Arduino Uno (Rev3) - ICSP

nets:
  VCC: HC-SR04_Sensor_1.VCC, Part1.5V
  N1: HC-SR04_Sensor_1.TRIG, Part1.ICSP_MISO, Part1.D12/MISO
  N2: HC-SR04_Sensor_1.ECHO, Part1.D11_PWM/MOSI
  GND: HC-SR04_Sensor_1.GND, J1.pin1, LED1.cathode, LED2.cathode, LED3.cathode, Part1.GND
  N3: J1.pin2, Part1.D10_PWM/SS
  N4: LED1.anode, Part1.D7
  N5: LED2.anode, Part1.D8
  N6: LED3.anode, Part1.D9_PWM
